# Fritzing sketch encoders_fritzing_diagram (saved by Fritzing 0.8.3b)
breadboards: 1

parts:
  Q1 = PHOTOTRANSISTOR REFLECTIVE OBJECT SENSOR [package=qrb1114-side]
  Part1 = Arduino Uno (Rev3)
  R1 = Resistor [tolerance=±5% resistance=10k package=THT]
  R2 = Resistor [tolerance=±5% resistance=100 package=THT]

nets:
  N1: Q1.A, Part1.GND, R1.Pin_0
  N2: Q1.C, Part1.5V, R2.Pin_1
  N3: Q1.E, Part1.D8, R1.Pin_1
